// Logisim project 16-Bit Single Circuit.circ as structural Verilog: 4 circuits, main circuit ALU
module ALU (
  input  [15:0] A,
  input  [15:0] B,
  input  in_3,
  input  Binv,
  input  [1:0] ALUop,
  output [15:0] Ruselt,
  output out_7,
  output Zero
);

  wire comparator_1_lt;
  wire [3:0] bit_extender_1_out;
  wire [15:0] adder_1_out, and_1_out, bit_extender_2_out, multiplexer_1_out, not_1_out, shifter_1_out;

  assign not_1_out = ~B;  // NOT_Gate not_1, 16 bits wide
  Multiplexer #(.width(16)) multiplexer_1 (.in0(B), .in1(not_1_out), .out(multiplexer_1_out), .sel(Binv));  // open: en
  Bit_Extender #(.in_width(16), .out_width(4)) bit_extender_1 (.in(multiplexer_1_out), .out(bit_extender_1_out));
  Adder #(.width(16)) adder_1 (.a(A), .b(multiplexer_1_out), .out(adder_1_out), .cin(in_3), .cout(out_7));
  assign and_1_out = A & multiplexer_1_out;  // AND_Gate and_1, 16 bits wide
  Comparator #(.width(16)) comparator_1 (.a(A), .b(multiplexer_1_out), .lt(comparator_1_lt));  // open: gt, eq
  Shifter #(.width(16)) shifter_1 (.in(A), .\dist (bit_extender_1_out), .out(shifter_1_out));
  assign bit_extender_2_out = {{15{1'b0}}, comparator_1_lt};  // Bit_Extender bit_extender_2
  Multiplexer #(.select(2), .width(16)) multiplexer_2 (
    .in0(adder_1_out), .in1(and_1_out), .in2(bit_extender_2_out), .in3(shifter_1_out), .out(Ruselt),
    .sel(ALUop));  // open: en
  nor nor_1 (Zero, Ruselt[0], Ruselt[1], Ruselt[2], Ruselt[3], Ruselt[4], Ruselt[5], Ruselt[6], Ruselt[7], Ruselt[8], Ruselt[9], Ruselt[10], Ruselt[11], Ruselt[12], Ruselt[13], Ruselt[14], Ruselt[15]);
endmodule

module Control_Unit (
  input  [3:0] in_1,
  output RegWrite,
  output RD_IM,
  output Binvert,
  output Cin,
  output [1:0] ALUop,
  output Mem_to_Reg,
  output Branch,
  output Jump,
  output Load,
  output Store,
  output RegDest
);

  wire add1001_out, addi0011_out, and0110_out, sll1000_out, slt0111_out, sub0100_out;

  and sw0000 (Store, ~in_1[3], ~in_1[2], ~in_1[1], ~in_1[0]);  // AND_Gate
  and lw0001 (Load, ~in_1[3], ~in_1[2], ~in_1[1], in_1[0]);  // AND_Gate
  and beq0010 (Branch, ~in_1[3], ~in_1[2], in_1[1], ~in_1[0]);  // AND_Gate
  and addi0011 (addi0011_out, ~in_1[3], ~in_1[2], in_1[1], in_1[0]);  // AND_Gate
  and sub0100 (sub0100_out, ~in_1[3], in_1[2], ~in_1[1], ~in_1[0]);  // AND_Gate
  and jmp0101 (Jump, ~in_1[3], in_1[2], ~in_1[1], in_1[0]);  // AND_Gate
  and and0110 (and0110_out, ~in_1[3], in_1[2], in_1[1], ~in_1[0]);  // AND_Gate
  and slt0111 (slt0111_out, ~in_1[3], in_1[2], in_1[1], in_1[0]);  // AND_Gate
  and sll1000 (sll1000_out, in_1[3], ~in_1[2], ~in_1[1], ~in_1[0]);  // AND_Gate
  and add1001 (add1001_out, in_1[3], ~in_1[2], ~in_1[1], in_1[0]);  // AND_Gate
  or or_1 (Binvert, sub0100_out, Branch);
  or or_2 (Cin, sub0100_out, Branch);
  or or_3 (ALUop[0], and0110_out, sll1000_out);
  or or_4 (ALUop[1], slt0111_out, sll1000_out);
  or or_5 (RegDest, Branch, sub0100_out, and0110_out, slt0111_out, sll1000_out, add1001_out);
  or or_6 (RegWrite, Load, addi0011_out, sub0100_out, and0110_out, slt0111_out, sll1000_out, add1001_out);
  or or_7 (RD_IM, Store, Load, addi0011_out, Jump);

  assign Mem_to_Reg = Load;
endmodule

module Register_File (
  input  [3:0] RS,
  input  [3:0] RT,
  input  [15:0] WriteData,
  input  CLK,
  input  [3:0] RD,
  input  RegWrite,
  output [15:0] DataRS,
  output [15:0] DataRT
);

  wire decoder_1_out0, decoder_1_out1, decoder_1_out2, decoder_1_out3, decoder_1_out4, decoder_1_out5,
       decoder_1_out6, decoder_1_out7, decoder_1_out8, decoder_1_out9, decoder_1_out10, decoder_1_out11,
       decoder_1_out12, decoder_1_out13, decoder_1_out14, decoder_1_out15;
  wire [15:0] R0_q, R1_q, R2_q, R3_q, R4_q, R5_q, R6_q, R7_q, R8_q, R9_q, R10_q, R11_q, R12_q, R13_q, R14_q,
       R15_q;

  Decoder #(.select(4), .disabled(0)) decoder_1 (
    .out0(decoder_1_out0), .out1(decoder_1_out1), .out2(decoder_1_out2), .out3(decoder_1_out3),
    .out4(decoder_1_out4), .out5(decoder_1_out5), .out6(decoder_1_out6), .out7(decoder_1_out7),
    .out8(decoder_1_out8), .out9(decoder_1_out9), .out10(decoder_1_out10), .out11(decoder_1_out11),
    .out12(decoder_1_out12), .out13(decoder_1_out13), .out14(decoder_1_out14), .out15(decoder_1_out15),
    .sel(RD), .en(RegWrite));
  Register #(.width(16)) R0 (.D(WriteData), .en(decoder_1_out0), .Q(R0_q), .clk(CLK));  // open: clr
  Register #(.width(16)) R1 (.D(WriteData), .en(decoder_1_out1), .Q(R1_q), .clk(CLK));  // open: clr
  Register #(.width(16)) R2 (.D(WriteData), .en(decoder_1_out2), .Q(R2_q), .clk(CLK));  // open: clr
  Register #(.width(16)) R3 (.D(WriteData), .en(decoder_1_out3), .Q(R3_q), .clk(CLK));  // open: clr
  Register #(.width(16)) R4 (.D(WriteData), .en(decoder_1_out4), .Q(R4_q), .clk(CLK));  // open: clr
  Register #(.width(16)) R5 (.D(WriteData), .en(decoder_1_out5), .Q(R5_q), .clk(CLK));  // open: clr
  Register #(.width(16)) R6 (.D(WriteData), .en(decoder_1_out6), .Q(R6_q), .clk(CLK));  // open: clr
  Register #(.width(16)) R7 (.D(WriteData), .en(decoder_1_out7), .Q(R7_q), .clk(CLK));  // open: clr
  Register #(.width(16)) R8 (.D(WriteData), .en(decoder_1_out8), .Q(R8_q), .clk(CLK));  // open: clr
  Register #(.width(16)) R9 (.D(WriteData), .en(decoder_1_out9), .Q(R9_q), .clk(CLK));  // open: clr
  Register #(.width(16)) R10 (.D(WriteData), .en(decoder_1_out10), .Q(R10_q), .clk(CLK));  // open: clr
  Register #(.width(16)) R11 (.D(WriteData), .en(decoder_1_out11), .Q(R11_q), .clk(CLK));  // open: clr
  Register #(.width(16)) R12 (.D(WriteData), .en(decoder_1_out12), .Q(R12_q), .clk(CLK));  // open: clr
  Register #(.width(16)) R13 (.D(WriteData), .en(decoder_1_out13), .Q(R13_q), .clk(CLK));  // open: clr
  Register #(.width(16)) R14 (.D(WriteData), .en(decoder_1_out14), .Q(R14_q), .clk(CLK));  // open: clr
  Register #(.width(16)) R15 (.D(WriteData), .en(decoder_1_out15), .Q(R15_q), .clk(CLK));  // open: clr
  Multiplexer #(.select(4), .width(16)) multiplexer_1 (
    .in0(R0_q), .in1(R1_q), .in2(R2_q), .in3(R3_q), .in4(R4_q), .in5(R5_q), .in6(R6_q), .in7(R7_q),
    .in8(R8_q), .in9(R9_q), .in10(R10_q), .in11(R11_q), .in12(R12_q), .in13(R13_q), .in14(R14_q),
    .in15(R15_q), .out(DataRS), .sel(RS));  // open: en
  Multiplexer #(.select(4), .width(16)) multiplexer_2 (
    .in0(R0_q), .in1(R1_q), .in2(R2_q), .in3(R3_q), .in4(R4_q), .in5(R5_q), .in6(R6_q), .in7(R7_q),
    .in8(R8_q), .in9(R9_q), .in10(R10_q), .in11(R11_q), .in12(R12_q), .in13(R13_q), .in14(R14_q),
    .in15(R15_q), .out(DataRT), .sel(RT));  // open: en
endmodule

module DataPath (
  output [3:0] Opcode,
  output [3:0] RS,
  output [3:0] RT,
  output [3:0] RD_Im,
  output [15:0] out_5
);

  wire alu_1_zero, and_1_out, clock_1_out, control_unit_1_binvert, control_unit_1_branch, control_unit_1_cin,
       control_unit_1_jump, control_unit_1_load, control_unit_1_mem_to_reg, control_unit_1_rd_im,
       control_unit_1_regdest, control_unit_1_regwrite, control_unit_1_store;
  wire [1:0] control_unit_1_aluop;
  wire [3:0] multiplexer_1_out;
  wire [15:0] adder_1_out, adder_2_out, alu_1_ruselt, bit_extender_1_out, bit_extender_2_out,
       multiplexer_2_out, multiplexer_3_out, multiplexer_4_out, ram_1_data, register_1_q,
       register_file_1_datars, register_file_1_datart;

  Register #(.width(16)) register_1 (.D(multiplexer_4_out), .Q(register_1_q), .clk(clock_1_out));  // open: en, clr
  Clock clock_1 (.out(clock_1_out));
  Adder #(.width(16)) adder_1 (.a(register_1_q), .b(16'h1), .out(adder_1_out), .cin(1'b0));  // open: cout
  Control_Unit control_unit_1 (
    .in_1(Opcode), .RegWrite(control_unit_1_regwrite), .RD_IM(control_unit_1_rd_im),
    .Binvert(control_unit_1_binvert), .Cin(control_unit_1_cin), .ALUop(control_unit_1_aluop),
    .Mem_to_Reg(control_unit_1_mem_to_reg), .Branch(control_unit_1_branch), .Load(control_unit_1_load),
    .Store(control_unit_1_store), .Jump(control_unit_1_jump), .RegDest(control_unit_1_regdest));
  ROM #(.addrWidth(16), .dataWidth(16)) rom_1 (.addr(register_1_q), .data({Opcode, RS, RT, RD_Im}));  // open: sel
  Multiplexer #(.width(4)) multiplexer_1 (
    .in0(RT), .in1(RD_Im), .out(multiplexer_1_out), .sel(control_unit_1_regdest));  // open: en
  Register_File register_file_1 (
    .WriteData(out_5), .CLK(clock_1_out), .RD(multiplexer_1_out), .RegWrite(control_unit_1_regwrite),
    .DataRS(register_file_1_datars), .RS(RS), .DataRT(register_file_1_datart), .RT(RT));
  assign bit_extender_1_out = {{12{1'b0}}, RD_Im};  // Bit_Extender bit_extender_1
  assign bit_extender_2_out = {{4{1'b0}}, {RS, RT, RD_Im}};  // Bit_Extender bit_extender_2
  Multiplexer #(.width(16)) multiplexer_2 (
    .in0(register_file_1_datart), .in1(bit_extender_1_out), .out(multiplexer_2_out),
    .sel(control_unit_1_rd_im));  // open: en
  ALU alu_1 (
    .in_3(control_unit_1_cin), .Ruselt(alu_1_ruselt), .ALUop(control_unit_1_aluop),
    .A(register_file_1_datars), .B(multiplexer_2_out), .Binv(control_unit_1_binvert), .Zero(alu_1_zero));  // open: out_7
  Adder #(.width(16)) adder_2 (.a(adder_1_out), .b(bit_extender_1_out), .out(adder_2_out));  // open: cin, cout
  and and_1 (and_1_out, alu_1_zero, control_unit_1_branch);
  Multiplexer #(.width(16)) multiplexer_3 (
    .in0(adder_1_out), .in1(adder_2_out), .out(multiplexer_3_out), .sel(and_1_out));  // open: en
  RAM #(.addrWidth(16), .dataWidth(16), .bus("separate")) ram_1 (
    .addr(alu_1_ruselt), .din(register_file_1_datart), .data(ram_1_data), .str(control_unit_1_store),
    .clk(clock_1_out), .ld(control_unit_1_load));  // open: sel, clr
  Multiplexer #(.width(16)) multiplexer_4 (
    .in0(multiplexer_3_out), .in1(bit_extender_2_out), .out(multiplexer_4_out), .sel(control_unit_1_jump));  // open: en
  Multiplexer #(.width(16)) multiplexer_5 (
    .in0(alu_1_ruselt), .in1(ram_1_data), .out(out_5), .sel(control_unit_1_mem_to_reg));  // open: en
endmodule
